# Fritzing sketch Wifi-SKR (saved by Fritzing 0.9.4)
circuit board: 6.07159cm x 3.48141cm
perfboards: 1

parts:
  R6 = Resistor [tolerance=±5% resistance=470 package=THT]
  JP1 = Header 5x2 [package=2x5-ra]
  JP2 = Header 5x2 [package=2x5-ra]
  R7 = Resistor [tolerance=±5% resistance=2.2k package=THT]
  R5 = Resistor [tolerance=±5% resistance=2.2k package=THT]
  WeMos_D1_Mini1 = WeMos D1 Mini
  R1 = Resistor [tolerance=±5% resistance=2.2k package=THT]
  R2 = Resistor [tolerance=±5% resistance=47 package=THT]
  R3 = Resistor [tolerance=±5% resistance=47 package=THT]
  R4 = Resistor [tolerance=±5% resistance=47 package=THT]

nets:
  N1: R6.Pin_0, JP1.4
  N2: R6.Pin_1, R7.Pin_1, WeMos_D1_Mini1.RST
  N3: JP1.5, R2.Pin_1
  N4: JP1.7, R1.Pin_1
  N5: JP1.9, R4.Pin_0
  N6: JP1.10, R3.Pin_0
  N7: JP2.1, WeMos_D1_Mini1.5V
  N8: JP2.2, R7.Pin_0, WeMos_D1_Mini1.G
  N9: JP2.9, R5.Pin_1
  N10: JP2.10, WeMos_D1_Mini1.D2
  N11: R5.Pin_0, WeMos_D1_Mini1.D3
  N12: WeMos_D1_Mini1.D5, R4.Pin_1
  N13: WeMos_D1_Mini1.D6, R3.Pin_1
  N14: WeMos_D1_Mini1.D7, R2.Pin_0
  N15: WeMos_D1_Mini1.D8, R1.Pin_0
